# Fritzing sketch Final (saved by Fritzing 0.9.5d)
circuit board: 8.46667cm x 5.64444cm

parts:
  U1 = ESP32-38PinWide [part_number=ESP32-38PinWide]
  Mod1 = Raspberry Pi Pico
  U4 = LIPO-1000mAh [package=lipo-1000]  # not connected
  M1 = fc-51 [package=THT]
  M2 = fc-51 [package=THT]
  M3 = fc-51 [package=THT]
  M4 = fc-51 [package=THT]
  M6 = DC Motor
  motorcontrollerDRI1 = motorcontrollerDRI0002
  Part1 = VL530X Time of Flight Distance Sensor [part_number="tonetoys #3317"]
  Buck_Convertor1 = Buck Convertor [part_number=LM2596 package=THT]
  Bat1 = Battery block 9V
  M7 = DC Motor
  U5 = RFID RC522 SIP - 8 pins [chip_label="RFID RC522" package="SIP (Single Inline) [THT]"]

nets:
  N1: U1.GPIO36, M3.pin1
  N2: U1.GPIO39, M4.pin1
  N3: U1.GPIO34, M1.pin1
  N4: U1.GPIO35, M2.pin1
  N5: U1.GPIO32, Mod1.pin_21
  N6: U1.GPIO33, Mod1.pin_22
  N7: U1.GPIO14, Mod1.pin_24
  GND: U1.GND, U1.GPIO11, Mod1.pin_13, Mod1.pin_23, Mod1.pin_38, M1.pin2, M2.pin2, M3.pin2, M4.pin2, Part1.GND, Buck_Convertor1.Negative_Output, U5.GND
  N8: U1.GPIO13, Mod1.pin_25
  VCC: U1.VIN, Mod1.pin_40, M1.pin3, M2.pin3, M3.pin3, M4.pin3, Part1.VCC, Buck_Convertor1.Positive_Output, U5.VCC
  N9: U1.GPIO4, U5.RST
  N10: U1.GPIO5, U5.NSS
  N11: U1.GPIO18, U5.SCK
  N12: U1.GPIO19, U5.MISO
  N13: U1.GPIO21, Part1.SDA
  N14: U1.GPIO22, Part1.SCL
  N15: U1.GPIO23, U5.MOSI
  N16: Mod1.pin_4, motorcontrollerDRI1.M1
  N17: Mod1.pin_5, motorcontrollerDRI1.E1
  N18: Mod1.pin_6, motorcontrollerDRI1.M2
  N19: Mod1.pin_7, motorcontrollerDRI1.E2
  N20: Mod1.pin_39, motorcontrollerDRI1.VS
  N21: M6.pin_1, motorcontrollerDRI1.M1-
  N22: M6.pin_2, motorcontrollerDRI1.M1+
  N23: motorcontrollerDRI1.VD, Buck_Convertor1.Positive_Input, Bat1.+
  N24: motorcontrollerDRI1.GND, Buck_Convertor1.Negative_Input, Bat1.-
  N25: motorcontrollerDRI1.M2+, M7.pin_1
  N26: motorcontrollerDRI1.M2-, M7.pin_2

custom parts:
  ESP32-38PinWide: Generic 38-Pin ESP32 with wide format (only access to one side of pins on a breadboard) based on Stephen Lilley's HiLetgo ESP-WROOM-32 ESP32 ESP-32S Development Board.
  Raspberry Pi Pico: Raspberry Pi Pico. Based around the RP2040 microcontroller the Pico is a low cost microcontroller device bringing Raspberry Pi quality, cost, and easy of use to the microcontroller space. Jan 2021, Split part in to two versions: SMD (this one) and tht. This one is single sided and uses the castellation pads to solder the module to the board (no holes, other than for the USB connector!). The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
  VL530X Time of Flight Distance Sensor: Time of flight sensor
  Buck Convertor: DC to DC buck convertor
  RFID RC522 SIP - 8 pins: A SIP stand-in part for RFID RC522 . With 8 pins on a 300 mil single inline package (SIP) footprint.
